# Fritzing sketch DP S02 01 (saved by Fritzing 0.9.3b)
circuit board: 10.2cm x 10cm
breadboards: 1

parts:
  U11 = ESP8266 WiFi Module [part_number=ESP8266]
  U12 = ESP8266 WiFi Module [part_number=ESP8266]
  U13 = ESP8266 WiFi Module [part_number=ESP8266]
  U14 = ESP8266 WiFi Module [part_number=ESP8266]
  RELAY20 = OMRON PCB Power Relay – G5LE [part_number="G5LE-1\n" package=THT]
  RELAY21 = OMRON PCB Power Relay – G5LE [part_number="G5LE-1\n" package=THT]
  RELAY22 = OMRON PCB Power Relay – G5LE [part_number="G5LE-1\n" package=THT]
  RELAY23 = OMRON PCB Power Relay – G5LE [part_number="G5LE-1\n" package=THT]
  RELAY24 = OMRON PCB Power Relay – G5LE [part_number="G5LE-1\n" package=THT]
  RELAY25 = OMRON PCB Power Relay – G5LE [part_number="G5LE-1\n" package=THT]
  RELAY26 = OMRON PCB Power Relay – G5LE [part_number="G5LE-1\n" package=THT]
  RELAY27 = OMRON PCB Power Relay – G5LE [part_number="G5LE-1\n" package=THT]
  OUT10 = screw terminal, 3 pins
  OUT11 = screw terminal, 3 pins
  OUT12 = screw terminal, 3 pins
  OUT13 = screw terminal, 3 pins
  OUT14 = screw terminal, 3 pins
  OUT15 = screw terminal, 3 pins
  OUT16 = screw terminal, 3 pins
  OUT17 = screw terminal, 3 pins
  IN2_IO7 = screw terminal, 2 pins
  IN2_IO8 = screw terminal, 2 pins
  IN2_IO9 = screw terminal, 2 pins
  IN2_IO10 = screw terminal, 2 pins
  IN1_TX5 = screw terminal, 2 pins
  IN1_TX6 = screw terminal, 2 pins
  IN1_TX7 = screw terminal, 2 pins
  IN1_TX8 = screw terminal, 2 pins
  N2008 = ULN2003A [package="DIP16 [THT]"]
  N2009 = ULN2003A [package="DIP16 [THT]"]
  N2010 = ULN2003A [package="DIP16 [THT]"]
  N2011 = ULN2003A [package="DIP16 [THT]"]
  IN7 = screw terminal, 2 pins
  IN8 = screw terminal, 2 pins
  IN9 = screw terminal, 2 pins
  IN10 = screw terminal, 2 pins
  3_3V5 = Voltage Regulator [package=to220-adj]
  3_3V6 = Voltage Regulator [package=to220-adj]
  3_3V7 = Voltage Regulator [package=to220-adj]
  3_3V8 = Voltage Regulator [package=to220-adj]

nets:
  N1: U11.RXD, N2011.Out_7
  N2: U11.VCC, U11.CH_PD, 3_3V8.OUT
  N3: U11.GPIO_0, N2011.Out_6
  N4: U11.GPIO_2, IN2_IO8.pin2
  N5: U11.GND, IN2_IO8.pin1, IN1_TX8.pin1, N2011.0V, IN7.pin2, 3_3V8.ADJ
  N6: U11.TXD, IN1_TX8.pin2
  N7: U12.RXD, N2009.Out_7
  N8: U12.VCC, U12.CH_PD, 3_3V5.OUT
  N9: U12.GPIO_0, N2009.Out_6
  N10: U12.GPIO_2, IN2_IO10.pin2
  N11: U12.GND, IN2_IO10.pin1, IN1_TX5.pin1, N2009.0V, IN9.pin2, 3_3V5.ADJ
  N12: U12.TXD, IN1_TX5.pin2
  N13: U13.RXD, N2008.Out_7
  N14: U13.VCC, U13.CH_PD, 3_3V7.OUT
  N15: U13.GPIO_0, N2008.Out_6
  N16: U13.GPIO_2, IN2_IO9.pin2
  N17: U13.GND, IN2_IO9.pin1, IN1_TX7.pin1, N2008.0V, IN10.pin2, 3_3V7.ADJ
  N18: U13.TXD, IN1_TX7.pin2
  N19: U14.RXD, N2010.Out_7
  N20: U14.VCC, U14.CH_PD, 3_3V6.OUT
  N21: U14.GPIO_0, N2010.Out_6
  N22: U14.GPIO_2, IN2_IO7.pin2
  N23: U14.GND, IN2_IO7.pin1, IN1_TX6.pin1, N2010.0V, IN8.pin2, 3_3V6.ADJ
  N24: U14.TXD, IN1_TX6.pin2
  N25: RELAY20.A, OUT13.pin1
  N26: RELAY20.COIL1, RELAY24.COIL2, N2011.COM_-_Common, IN7.pin1, 3_3V8.IN
  N27: RELAY20.C, OUT13.pin2
  N28: RELAY20.COIL2, N2011.In_6
  N29: RELAY20.B, OUT13.pin3
  N30: RELAY21.A, OUT12.pin1
  N31: RELAY21.COIL1, RELAY27.COIL2, N2009.COM_-_Common, IN9.pin1, 3_3V5.IN
  N32: RELAY21.C, OUT12.pin2
  N33: RELAY21.COIL2, N2009.In_6
  N34: RELAY21.B, OUT12.pin3
  N35: RELAY22.A, OUT11.pin1
  N36: RELAY22.COIL1, RELAY26.COIL2, N2008.COM_-_Common, IN10.pin1, 3_3V7.IN
  N37: RELAY22.C, OUT11.pin2
  N38: RELAY22.COIL2, N2008.In_6
  N39: RELAY22.B, OUT11.pin3
  N40: RELAY23.A, OUT10.pin1
  N41: RELAY23.COIL1, RELAY25.COIL2, N2010.COM_-_Common, IN8.pin1, 3_3V6.IN
  N42: RELAY23.C, OUT10.pin2
  N43: RELAY23.COIL2, N2010.In_6
  N44: RELAY23.B, OUT10.pin3
  N45: RELAY24.A, OUT16.pin1
  N46: RELAY24.COIL1, N2011.In_7
  N47: RELAY24.C, OUT16.pin2
  N48: RELAY24.B, OUT16.pin3
  N49: RELAY25.A, OUT17.pin1
  N50: RELAY25.COIL1, N2010.In_7
  N51: RELAY25.C, OUT17.pin2
  N52: RELAY25.B, OUT17.pin3
  N53: RELAY26.A, OUT14.pin1
  N54: RELAY26.COIL1, N2008.In_7
  N55: RELAY26.C, OUT14.pin2
  N56: RELAY26.B, OUT14.pin3
  N57: RELAY27.A, OUT15.pin1
  N58: RELAY27.COIL1, N2009.In_7
  N59: RELAY27.C, OUT15.pin2
  N60: RELAY27.B, OUT15.pin3

notes:
  Made in egypt
  DP S02
  -
  DP COMPANY
  +

custom parts:
  ESP8266 WiFi Module: Generic WiFi Module based on the ESP8266 with onboard PCB antenna and UART communications
