# Fritzing sketch DP S02 (saved by Fritzing 0.9.3b)
circuit board: 10.2cm x 10.5cm
breadboards: 1

parts:
  U1 = ESP8266 WiFi Module [part_number=ESP8266]
  RELAY1 = OMRON PCB Power Relay – G5LE [part_number="G5LE-1\n" package=THT]
  OUT0 = screw terminal, 3 pins
  OUT1 = screw terminal, 3 pins
  IN2_IO2 = screw terminal, 2 pins
  IN1_TX = screw terminal, 2 pins
  RELAY0 = OMRON PCB Power Relay – G5LE [part_number="G5LE-1\n" package=THT]
  N2003 = ULN2003A [package="DIP16 [THT]"]
  IN1 = screw terminal, 2 pins
  U2 = Voltage Regulator [package=to220-adj]
  U3 = ESP8266 WiFi Module [part_number=ESP8266]
  RELAY1_2 = OMRON PCB Power Relay – G5LE [part_number="G5LE-1\n" package=THT]
  RELAY0_2 = OMRON PCB Power Relay – G5LE [part_number="G5LE-1\n" package=THT]
  OUT0_2 = screw terminal, 3 pins
  OUT1_2 = screw terminal, 3 pins
  IN2_IO2_2 = screw terminal, 2 pins
  IN1_TX_2 = screw terminal, 2 pins
  N2003_2 = ULN2003A [package="DIP16 [THT]"]
  IN2 = screw terminal, 2 pins
  U4 = Voltage Regulator [package=to220-adj]
  U5 = ESP8266 WiFi Module [part_number=ESP8266]
  U6 = ESP8266 WiFi Module [part_number=ESP8266]
  RELAY10 = OMRON PCB Power Relay – G5LE [part_number="G5LE-1\n" package=THT]
  RELAY11 = OMRON PCB Power Relay – G5LE [part_number="G5LE-1\n" package=THT]
  RELAY2 = OMRON PCB Power Relay – G5LE [part_number="G5LE-1\n" package=THT]
  RELAY1_3 = OMRON PCB Power Relay – G5LE [part_number="G5LE-1\n" package=THT]
  OUT0_3 = screw terminal, 3 pins
  OUT0_4 = screw terminal, 3 pins
  OUT1_3 = screw terminal, 3 pins
  OUT1_4 = screw terminal, 3 pins
  IN2_IO2_3 = screw terminal, 2 pins
  IN2_IO2_4 = screw terminal, 2 pins
  IN1_TX_3 = screw terminal, 2 pins
  IN1_TX_4 = screw terminal, 2 pins
  N2003_3 = ULN2003A [package="DIP16 [THT]"]
  N2003_4 = ULN2003A [package="DIP16 [THT]"]
  IN = screw terminal, 2 pins
  IN_2 = screw terminal, 2 pins
  3_3V = Voltage Regulator [package=to220-adj]
  3_3V_2 = Voltage Regulator [package=to220-adj]

nets:
  N1: U1.RXD, N2003.Out_7
  N2: U1.VCC, U1.CH_PD, U2.OUT
  N3: U1.GPIO_0, N2003.Out_6
  N4: U1.GPIO_2, IN2_IO2.pin2
  N5: U1.GND, IN2_IO2.pin1, IN1_TX.pin1, N2003.0V, IN1.pin2, U2.ADJ
  N6: U1.TXD, IN1_TX.pin2
  N7: RELAY1.A, OUT1.pin1
  N8: RELAY1.COIL1, N2003.In_7
  N9: RELAY1.C, OUT1.pin2
  N10: RELAY1.COIL2, RELAY0.COIL1, N2003.COM_-_Common, IN1.pin1, U2.IN
  N11: RELAY1.B, OUT1.pin3
  N12: OUT0.pin1, RELAY0.A
  N13: OUT0.pin2, RELAY0.C
  N14: OUT0.pin3, RELAY0.B
  N15: RELAY0.COIL2, N2003.In_6
  N16: U3.RXD, N2003_2.Out_7
  N17: U3.VCC, U3.CH_PD, U4.OUT
  N18: U3.GPIO_0, N2003_2.Out_6
  N19: U3.GPIO_2, IN2_IO2_2.pin2
  N20: U3.GND, IN2_IO2_2.pin1, IN1_TX_2.pin1, N2003_2.0V, IN2.pin2, U4.ADJ
  N21: U3.TXD, IN1_TX_2.pin2
  N22: RELAY1_2.A, OUT1_2.pin1
  N23: RELAY1_2.COIL1, N2003_2.In_7
  N24: RELAY1_2.C, OUT1_2.pin2
  N25: RELAY1_2.COIL2, RELAY0_2.COIL1, N2003_2.COM_-_Common, IN2.pin1, U4.IN
  N26: RELAY1_2.B, OUT1_2.pin3
  N27: RELAY0_2.A, OUT0_2.pin1
  N28: RELAY0_2.C, OUT0_2.pin2
  N29: RELAY0_2.COIL2, N2003_2.In_6
  N30: RELAY0_2.B, OUT0_2.pin3
  N31: U5.RXD, N2003_3.Out_7
  N32: U5.VCC, U5.CH_PD, 3_3V.OUT
  N33: U5.GPIO_0, N2003_3.Out_6
  N34: U5.GPIO_2, IN2_IO2_3.pin2
  N35: U5.GND, IN2_IO2_3.pin1, IN1_TX_3.pin1, N2003_3.0V, IN.pin2, 3_3V.ADJ
  N36: U5.TXD, IN1_TX_3.pin2
  N37: U6.RXD, N2003_4.Out_7
  N38: U6.VCC, U6.CH_PD, 3_3V_2.OUT
  N39: U6.GPIO_0, N2003_4.Out_6
  N40: U6.GPIO_2, IN2_IO2_4.pin2
  N41: U6.GND, IN2_IO2_4.pin1, IN1_TX_4.pin1, N2003_4.0V, IN_2.pin2, 3_3V_2.ADJ
  N42: U6.TXD, IN1_TX_4.pin2
  N43: RELAY10.A, OUT0_3.pin1
  N44: RELAY10.COIL1, RELAY11.COIL2, N2003_3.COM_-_Common, IN.pin1, 3_3V.IN
  N45: RELAY10.C, OUT0_3.pin2
  N46: RELAY10.COIL2, N2003_3.In_6
  N47: RELAY10.B, OUT0_3.pin3
  N48: RELAY11.A, OUT1_3.pin1
  N49: RELAY11.COIL1, N2003_3.In_7
  N50: RELAY11.C, OUT1_3.pin2
  N51: RELAY11.B, OUT1_3.pin3
  N52: RELAY2.A, OUT0_4.pin1
  N53: RELAY2.COIL1, RELAY1_3.COIL2, N2003_4.COM_-_Common, IN_2.pin1, 3_3V_2.IN
  N54: RELAY2.C, OUT0_4.pin2
  N55: RELAY2.COIL2, N2003_4.In_6
  N56: RELAY2.B, OUT0_4.pin3
  N57: RELAY1_3.A, OUT1_4.pin1
  N58: RELAY1_3.COIL1, N2003_4.In_7
  N59: RELAY1_3.C, OUT1_4.pin2
  N60: RELAY1_3.B, OUT1_4.pin3

notes:
  -
  +
  DP COMPANY
  DP S02
  Made in egypt

custom parts:
  ESP8266 WiFi Module: Generic WiFi Module based on the ESP8266 with onboard PCB antenna and UART communications
